# Fritzing sketch mikrocontroller (saved by Fritzing 0.9.3b)
breadboards: 1

parts:
  Mikrocontroller = MICROCONTROLLER [package=dil28-3-zif_socket]
  EMG-Sensor = Grove Light Sensor
  Bluetooth-Chip = Bluetooth HC-05 Macho
  Quarz = CRYSTAL - kHz [frequency="16 MHz"]
  C1 = Ceramic Capacitor [capacitance=100nF package="100 mil [THT, multilayer]"]
  Kondensatoren = Ceramic Capacitor [capacitance=22pF package="100 mil [THT, multilayer]"]
  Batterie_4_5_V = Battery

nets:
  N1: Mikrocontroller.PC6(_RESET), Mikrocontroller.AVCC, EMG-Sensor.VCC
  N2: Mikrocontroller.PD0(RXD), Bluetooth-Chip.RXD
  N3: Mikrocontroller.PD1(TXD), Bluetooth-Chip.TXD
  VCC: Mikrocontroller.VCC, Mikrocontroller.AREF, Bluetooth-Chip.VCC, Batterie_4_5_V.+
  GND: Mikrocontroller.GND, Mikrocontroller.AGND, EMG-Sensor.GND, Bluetooth-Chip.GND, C1.0, Kondensatoren.0, Batterie_4_5_V.-
  N4: Mikrocontroller.PB6(XTAL1_TOSC1), Quarz.pin_1, Kondensatoren.1
  N5: Mikrocontroller.PB7(XTAL2_TOSC2), Quarz.pin_0, C1.1
  N6: Mikrocontroller.PC0(ADC0), EMG-Sensor.SIG
